# Fritzing sketch BelowDiagram (saved by Fritzing 0.9.3b)
breadboards: 1

parts:
  Part5 = MCP9808
  Part6 = Arduino Pro Mini v13
  J1 = male pin header, 4 pins [form="♂ (male)"]
  Part8 = Arduino Pro Mini (5V)  # not connected
  LED1 = LED - 3mm [color="Red (633nm)" package="3 mm [THT]"]
  R1 = Resistor [tolerance=±5% resistance=220 package="0402 [SMD]"]

nets:
  N1: Part5.SDA, Part6.A4
  N2: Part5.SCL, Part6.A5
  VCC: Part5.VCC, Part6.VCC, J1.pin2
  GND: Part5.GND, Part6.GND, J1.pin1, R1.Pin_1
  N3: Part6.D0/TX, J1.pin4
  N4: Part6.D1/RX, J1.pin3
  N5: Part6.D10_PWM/SS, LED1.cathode
  N6: LED1.anode, R1.Pin_0
