# Fritzing sketch SensorsDiagram (saved by Fritzing 0.9.3b)
breadboards: 1

parts:
  Part8 = Arduino Pro Mini (5V)
  Part10 = DeadOn RTC - DS3234 Breakout
  Part11 = HUZZAH ESP8266 Breakout
  microSD1 = MicroSD Breakout
  Part12 = USB Type A Female Breakout Board [part_number=BOB-12700]  # not connected
  Part13 = Arduino Pro Mini v13
  LED2 = LED - 3mm [color="Red (633nm)" package="3 mm [THT]"]
  R2 = Resistor [tolerance=±5% resistance=220 package="0402 [SMD]"]
  J2 = male pin header, 4 pins [form="♂ (male)"]
  Part14 = MCP9808

nets:
  N1: Part8.D8, Part10.SS
  N2: Part10.MOSI, microSD1.DI
  N3: Part10.MISO, microSD1.DO
  N4: Part10.SCLK, microSD1.CLK
  GND: Part10.INT/SQW, Part10.GND, Part11.GND, microSD1.GND, Part13.GND, R2.Pin_0, J2.pin1, Part14.GND
  VCC: Part10.VCC, Part11.VIN, microSD1.5V, Part13.VCC, J2.pin2, Part14.VCC
  N5: Part13.D0/TX, J2.pin4
  N6: Part13.D1/RX, J2.pin3
  N7: Part13.A4, Part14.SDA
  N8: Part13.A5, Part14.SCL
  N9: Part13.D10_PWM/SS, LED2.cathode
  N10: LED2.anode, R2.Pin_1

custom parts:
  HUZZAH ESP8266 Breakout: The ESP8266 processor from Espressif is an 80 MHz microcontroller with a full WiFi front-end (both as client and access point) and TCP/IP stack with DNS support as well.
  MicroSD Breakout: 5V-ready microSD Breakout with Level Shifter
  USB Type A Female Breakout Board: USB breakout board for a Type A connector. sparkfun.com
