# Fritzing sketch enclosure (saved by Fritzing 0.9.3b)
breadboards: 1

parts:
  Part1 = Arduino Pro Mini (3.3V)
  R1 = Resistor [tolerance=±5% resistance=220 package=THT]
  LED1 = LED - 5mm [color="Red (633nm)" package="5 mm [THT]"]
  Part2 = Digital Temperature Sensor Breakout - TMP102

nets:
  N1: Part1.A4, Part2.SCL
  N2: Part1.A5, Part2.GND
  N3: R1.Pin_0, R1.Pin_1, LED1.cathode, Part2.V+
