# Fritzing sketch AboveDiagram (saved by Fritzing 0.9.3b)

parts:
  Part8 = Arduino Pro Mini (5V)
  Part10 = DeadOn RTC - DS3234 Breakout

nets:
  N1: Part8.SCK, Part10.SCLK
  N2: Part8.MISO, Part10.MISO
  N3: Part8.MOSI, Part10.MOSI
  N4: Part8.D8, Part10.SS
