# Fritzing sketch AboveSdDiagram (saved by Fritzing 0.9.3b)

parts:
  Part8 = Arduino Pro Mini (5V)
  microSD1 = MicroSD Breakout

nets:
  N1: Part8.SCK, microSD1.CLK
  N2: Part8.MISO, microSD1.DO
  N3: Part8.MOSI, microSD1.DI
  N4: Part8.D10, microSD1.CS

custom parts:
  MicroSD Breakout: 5V-ready microSD Breakout with Level Shifter
