# Fritzing sketch WifiDiagram (saved by Fritzing 0.9.3b)

parts:
  Part8 = Arduino Pro Mini (5V)
  Adafruit_HUZZAH_ESP8266_Breakout1 = Adafruit HUZZAH ESP8266 Breakout [part_number=2471]

nets:
  N1: Part8.TXO, Adafruit_HUZZAH_ESP8266_Breakout1.RX
  N2: Part8.RXI, Adafruit_HUZZAH_ESP8266_Breakout1.#14
